// Logisim project pra2.circ as structural Verilog: 1 circuit, main circuit main
module main (
  input  in_1,
  input  in_2,
  input  in_3,
  input  in_4,
  input  in_5,
  input  in_6,
  input  in_7,
  input  in_8,
  output out_9,
  output out_10,
  output out_11,
  output out_12
);

  wire not_1_out, not_2_out;

  not not_1 (not_1_out, in_3);
  not not_2 (not_2_out, in_7);
  or or_1 (out_9, in_1, in_2);
  or or_2 (out_10, not_1_out, in_4);
  and and_1 (out_11, in_5, in_6);
  and and_2 (out_12, not_2_out, in_8);

  // Notes on the sheet:
  //   practical no : 2
endmodule
