// Logisim project pra3.circ as structural Verilog: 1 circuit, main circuit main
module main (
  input  in_1,
  input  in_2,
  input  in_3,
  input  in_4,
  input  in_5,
  input  in_6,
  input  in_7,
  input  in_8,
  input  in_9,
  input  in_10,
  input  in_11,
  input  in_12,
  input  in_13,
  input  in_14,
  output out_15,
  output out_16,
  output out_17,
  output out_18,
  output out_19,
  output out_20,
  output out_21,
  output out_22
);

  wire nand_2_out, nand_3_out, nand_4_out, nand_5_out, nand_8_out, nand_9_out, nor_1_out, nor_2_out,
       nor_3_out, nor_4_out, nor_8_out, nor_9_out, nor_10_out;

  nand nand_1 (out_16, in_2, in_2);
  nand nand_2 (nand_2_out, in_4, in_4);
  nand nand_3 (nand_3_out, in_6, in_6);
  nand nand_4 (nand_4_out, in_8, in_10);
  nand nand_5 (nand_5_out, in_12, in_14);
  nand nand_6 (out_18, nand_2_out, nand_3_out);
  nand nand_7 (out_20, nand_4_out, nand_4_out);
  nand nand_8 (nand_8_out, in_12, nand_5_out);
  nand nand_9 (nand_9_out, nand_5_out, in_14);
  nand nand_10 (out_22, nand_8_out, nand_9_out);
  nor nor_1 (nor_1_out, in_3, in_5);
  nor nor_2 (nor_2_out, in_7, in_7);
  nor nor_3 (nor_3_out, in_9, in_9);
  nor nor_4 (nor_4_out, in_11, in_13);
  nor nor_5 (out_15, in_1, in_1);
  nor nor_6 (out_17, nor_1_out, nor_1_out);
  nor nor_7 (out_19, nor_2_out, nor_3_out);
  nor nor_8 (nor_8_out, in_11, nor_4_out);
  nor nor_9 (nor_9_out, nor_4_out, in_13);
  nor nor_10 (nor_10_out, nor_8_out, nor_9_out);
  nor nor_11 (out_21, nor_10_out, nor_10_out);

  // Notes on the sheet:
  //   practical no : 3
endmodule
